# Fritzing sketch smart_irrigation_circuit (saved by Fritzing 0.9.10b)
breadboards: 1

parts:
  Parça1 = Soil Moisture Sensor
  Mod1 = Heltec WiFi LoRa 32 V2 [part_number=HTIT-WB32LA]
  Grove1 = Grove OLED 128x96
  M1 = DC Motor [voltage_(max)=6V voltage_(min)=3V]
  Parça2 = Breadboard Power Supply Board SMD
  U2 = RELAY [package=relay-jzc]

nets:
  GND: Parça1.GND, Mod1.GND, Grove1.GND, M1.pin_2, Parça2.GND, U2.COIL2
  N1: Parça1.SIG, Mod1.pin_9
  VCC: Parça1.VCC, Mod1.pin_17, Grove1.VCC, Parça2.VCC, U2.NO, U2.COIL1
  N2: Mod1.pin_1, Grove1.SDA
  N3: Mod1.pin_7, U2.NC
  N4: Mod1.pin_21, Mod1.pin_22
  N5: Mod1.pin_27, Grove1.SCL
  N6: M1.pin_1, U2.MAIN
